# Fritzing sketch schieberegister_transistor_led (saved by Fritzing 0.9.9b)
breadboards: 1

parts:
  Q1 = TRANSISTOR_NPN [package=to-92]
  LED1 = LED - 5mm [color="Red (633nm)" current=0.030 package="5 mm [THT]"]
  R1 = Resistor [tolerance=±5% power=0.25 resistance=220 package=THT]
  R2 = Resistor [tolerance=±5% power=0.25 resistance=1k package=THT]

nets:
  N1: Q1.E, LED1.anode
  N2: Q1.B, R2.Pin_1
  N3: LED1.cathode, R1.Pin_1
