# Fritzing sketch schieberegister_transistor_led2 (saved by Fritzing 0.9.9b)
breadboards: 1

parts:
  Q1 = TRANSISTOR_NPN [package=to-92]
  LED1 = LED - 5mm [color="Red (633nm)" current=0.030 package="5 mm [THT]"]
  R1 = Resistor [tolerance=±5% power=0.25 resistance=220 package=THT]
  R2 = Resistor [tolerance=±5% power=0.25 resistance=1k package=THT]
  Q2 = TRANSISTOR_NPN [package=to-92]
  LED2 = LED - 5mm [color="Red (633nm)" current=0.030 package="5 mm [THT]"]
  R3 = Resistor [tolerance=±5% power=0.25 resistance=1k package=THT]
  R4 = Resistor [tolerance=±5% power=0.25 resistance=220 package=THT]
  Q3 = TRANSISTOR_NPN [package=to-92]
  LED3 = LED - 5mm [color="Red (633nm)" current=0.030 package="5 mm [THT]"]
  R5 = Resistor [tolerance=±5% power=0.25 resistance=1k package=THT]
  R6 = Resistor [tolerance=±5% power=0.25 resistance=220 package=THT]
  Q4 = TRANSISTOR_NPN [package=to-92]
  LED4 = LED - 5mm [color="Red (633nm)" current=0.030 package="5 mm [THT]"]
  R7 = Resistor [tolerance=±5% power=0.25 resistance=1k package=THT]
  R8 = Resistor [tolerance=±5% power=0.25 resistance=220 package=THT]
  U1 = 74HC595 [package="DIP16 [THT]"]
  Q5 = TRANSISTOR_NPN [package=to-92]
  Q6 = TRANSISTOR_NPN [package=to-92]
  Q7 = TRANSISTOR_NPN [package=to-92]
  Q8 = TRANSISTOR_NPN [package=to-92]
  LED5 = LED - 5mm [color="Red (633nm)" current=0.030 package="5 mm [THT]"]
  LED6 = LED - 5mm [color="Red (633nm)" current=0.030 package="5 mm [THT]"]
  LED7 = LED - 5mm [color="Red (633nm)" current=0.030 package="5 mm [THT]"]
  LED8 = LED - 5mm [color="Red (633nm)" current=0.030 package="5 mm [THT]"]
  R11 = Resistor [tolerance=±5% power=0.25 resistance=220 package=THT]
  R16 = Resistor [tolerance=±5% power=0.25 resistance=220 package=THT]
  R17 = Resistor [tolerance=±5% power=0.25 resistance=220 package=THT]
  R18 = Resistor [tolerance=±5% power=0.25 resistance=220 package=THT]
  R19 = Resistor [tolerance=±5% power=0.25 resistance=1k package=THT]
  R20 = Resistor [tolerance=±5% power=0.25 resistance=1k package=THT]
  R21 = Resistor [tolerance=±5% power=0.25 resistance=1k package=THT]
  R22 = Resistor [tolerance=±5% power=0.25 resistance=1k package=THT]
  Part1 = Arduino Uno (Rev3) - ICSP

nets:
  N1: Q1.E, LED1.anode
  N2: Q1.B, R2.Pin_1
  VCC: Q1.C, Q2.C, Q3.C, U1.MR, U1.VCC, Q5.C, Q6.C, Q7.C, Q8.C, Part1.5V
  N3: LED1.cathode, R1.Pin_1
  N4: R1.Pin_0, R4.Pin_0, R6.Pin_0, R8.Pin_0, U1.OE, R11.Pin_1, R16.Pin_1, R17.Pin_1, R18.Pin_1, Part1.GND
  N5: R2.Pin_0, U1.Q0
  N6: Q2.E, LED2.anode
  N7: Q2.B, R3.Pin_1
  N8: LED2.cathode, R4.Pin_1
  N9: R3.Pin_0, U1.Q1
  N10: Q3.E, LED3.anode
  N11: Q3.B, R5.Pin_1
  N12: LED3.cathode, R6.Pin_1
  N13: R5.Pin_0, U1.Q2
  N14: Q4.E, LED4.anode
  N15: LED4.cathode, R8.Pin_1
  N16: R7.Pin_0, U1.Q3
  N17: U1.Q4, R22.Pin_1
  N18: U1.Q5, R21.Pin_1
  N19: U1.Q6, R20.Pin_1
  N20: U1.Q7, R19.Pin_1
  N21: U1.SH_CP, Part1.D10_PWM/SS
  N22: U1.ST_CP, Part1.D9_PWM
  N23: U1.DS, Part1.D8
  N24: Q5.E, LED6.anode
  N25: Q5.B, R22.Pin_0
  N26: Q6.E, LED5.anode
  N27: Q6.B, R21.Pin_0
  N28: Q7.E, LED7.anode
  N29: Q7.B, R19.Pin_0
  N30: Q8.E, LED8.anode
  N31: Q8.B, R20.Pin_0
  N32: LED5.cathode, R16.Pin_0
  N33: LED6.cathode, R11.Pin_0
  N34: LED7.cathode, R18.Pin_0
  N35: LED8.cathode, R17.Pin_0
