# Fritzing sketch schieberegister_transistor_led3 (saved by Fritzing 0.9.9b)
circuit board: 14.1101cm x 4.02913cm
breadboards: 1

parts:
  R1 = Resistor [tolerance=±5% power=0.25 resistance=220 package=THT]
  R2 = Resistor [tolerance=±5% power=0.25 resistance=220 package=THT]
  PN2222A = TRANSISTOR_NPN [package=to-92-ammo]
  GROUND = Header 1 [package=smtso-256-et]
  GROUND_2 = Header 1 [package=smtso-256-et]
  5V = Header 1 [package=smtso-256-et]
  LED0 = LED - 5mm [color="Red (633nm)" current=0.030 package="5 mm [THT]"]
  R2_2 = Resistor [tolerance=±5% power=0.25 resistance=220 package=THT]
  R1_2 = Resistor [tolerance=±5% power=0.25 resistance=220 package=THT]
  PN2222A_2 = TRANSISTOR_NPN [package=to-92-ammo]
  LED1 = LED - 5mm [color="Red (633nm)" current=0.030 package="5 mm [THT]"]
  R2_3 = Resistor [tolerance=±5% power=0.25 resistance=220 package=THT]
  R1_3 = Resistor [tolerance=±5% power=0.25 resistance=220 package=THT]
  PN2222A_3 = TRANSISTOR_NPN [package=to-92-ammo]
  LED2 = LED - 5mm [color="Red (633nm)" current=0.030 package="5 mm [THT]"]
  R2_4 = Resistor [tolerance=±5% power=0.25 resistance=220 package=THT]
  R1_4 = Resistor [tolerance=±5% power=0.25 resistance=220 package=THT]
  PN2222A_4 = TRANSISTOR_NPN [package=to-92-ammo]
  LED3 = LED - 5mm [color="Red (633nm)" current=0.030 package="5 mm [THT]"]
  R2_5 = Resistor [tolerance=±5% power=0.25 resistance=220 package=THT]
  R1_5 = Resistor [tolerance=±5% power=0.25 resistance=220 package=THT]
  PN2222A_5 = TRANSISTOR_NPN [package=to-92-ammo]
  LED4 = LED - 5mm [color="Red (633nm)" current=0.030 package="5 mm [THT]"]
  R2_6 = Resistor [tolerance=±5% power=0.25 resistance=220 package=THT]
  R1_6 = Resistor [tolerance=±5% power=0.25 resistance=220 package=THT]
  PN2222A_6 = TRANSISTOR_NPN [package=to-92-ammo]
  LED5 = LED - 5mm [color="Red (633nm)" current=0.030 package="5 mm [THT]"]
  R2_7 = Resistor [tolerance=±5% power=0.25 resistance=220 package=THT]
  R1_7 = Resistor [tolerance=±5% power=0.25 resistance=220 package=THT]
  PN2222A_7 = TRANSISTOR_NPN [package=to-92-ammo]
  LED6 = LED - 5mm [color="Red (633nm)" current=0.030 package="5 mm [THT]"]
  R2_8 = Resistor [tolerance=±5% power=0.25 resistance=220 package=THT]
  R1_8 = Resistor [tolerance=±5% power=0.25 resistance=220 package=THT]
  PN2222A_8 = TRANSISTOR_NPN [package=to-92-ammo]
  LED7 = LED - 5mm [color="Red (633nm)" current=0.030 package="5 mm [THT]"]
  74HC595 = 74HC595 [package="DIP16 [THT]"]
  5V1 = Header 1 [package=smtso-256-et]
  5V2 = Header 1 [package=smtso-256-et]
  5V3 = Header 1 [package=smtso-256-et]

nets:
  N1: R1.Pin_0, GROUND.1, GROUND_2.1, R1_2.Pin_0, R1_3.Pin_0, R1_4.Pin_0, R1_5.Pin_0, R1_6.Pin_0, R1_7.Pin_0, R1_8.Pin_0, 74HC595.GND, 74HC595.OE
  N2: R1.Pin_1, LED0.cathode
  N3: R2.Pin_0, 74HC595.Q0
  N4: R2.Pin_1, PN2222A.B
  N5: PN2222A.E, LED0.anode
  N6: PN2222A.C, 5V.1, PN2222A_2.C, PN2222A_3.C, PN2222A_4.C, PN2222A_5.C, PN2222A_6.C, PN2222A_7.C, PN2222A_8.C, 74HC595.MR, 74HC595.VCC
  N7: R2_2.Pin_0, 74HC595.Q1
  N8: R2_2.Pin_1, PN2222A_2.B
  N9: R1_2.Pin_1, LED1.cathode
  N10: PN2222A_2.E, LED1.anode
  N11: R2_3.Pin_0, 74HC595.Q2
  N12: R2_3.Pin_1, PN2222A_3.B
  N13: R1_3.Pin_1, LED2.cathode
  N14: PN2222A_3.E, LED2.anode
  N15: R2_4.Pin_0, 74HC595.Q3
  N16: R2_4.Pin_1, PN2222A_4.B
  N17: R1_4.Pin_1, LED3.cathode
  N18: PN2222A_4.E, LED3.anode
  N19: R2_5.Pin_0, 74HC595.Q4
  N20: R2_5.Pin_1, PN2222A_5.B
  N21: R1_5.Pin_1, LED4.cathode
  N22: PN2222A_5.E, LED4.anode
  N23: R2_6.Pin_0, 74HC595.Q5
  N24: R2_6.Pin_1, PN2222A_6.B
  N25: R1_6.Pin_1, LED5.cathode
  N26: PN2222A_6.E, LED5.anode
  N27: R2_7.Pin_0, 74HC595.Q6
  N28: R2_7.Pin_1, PN2222A_7.B
  N29: R1_7.Pin_1, LED6.cathode
  N30: PN2222A_7.E, LED6.anode
  N31: R2_8.Pin_0, 74HC595.Q7
  N32: R2_8.Pin_1, PN2222A_8.B
  N33: R1_8.Pin_1, LED7.cathode
  N34: PN2222A_8.E, LED7.anode
  N35: 74HC595.SH_CP, 5V3.1
  N36: 74HC595.ST_CP, 5V2.1
  N37: 74HC595.DS, 5V1.1
